# Fritzing sketch grissom (saved by Fritzing 0.9.4)
breadboards: 1

parts:
  Q1 = NPN-Transistor [package="TO92 [THT]"]
  Q2 = NPN-Transistor [package="TO92 [THT]"]
  R1 = Resistor [tolerance=±5% resistance=100 package=THT]
  R2 = Resistor [tolerance=±5% resistance=100 package=THT]
  R3 = Resistor [tolerance=±5% resistance=100 package=THT]
  R4 = Resistor [tolerance=±5% resistance=100 package=THT]
  R5 = Resistor [tolerance=±5% resistance=100 package=THT]
  R6 = Resistor [tolerance=±5% resistance=100 package=THT]
  R7 = Resistor [tolerance=±5% resistance=100 package=THT]
  R8 = Resistor [tolerance=±5% resistance=100 package=THT]
  R9 = Resistor [tolerance=±5% resistance=100 package=THT]
  R10 = Resistor [tolerance=±5% resistance=100 package=THT]
  R11 = Resistor [tolerance=±5% resistance=100 package=THT]
  R12 = Resistor [tolerance=±5% resistance=100 package=THT]
  R13 = Resistor [tolerance=±5% resistance=100 package=THT]
  LED1 = LED - 3mm [color="Red (633nm)" package="3 mm [THT]"]
  LED2 = LED - 3mm [color="Red (633nm)" package="3 mm [THT]"]
  LED3 = LED - 3mm [color="Red (633nm)" package="3 mm [THT]"]
  LED4 = LED - 3mm [color="Red (633nm)" package="3 mm [THT]"]
  LED5 = LED - 3mm [color="Green (555nm)" package="3 mm [THT]"]
  LED6 = LED - 3mm [color="Green (555nm)" package="3 mm [THT]"]
  LED7 = LED - 3mm [color="Green (555nm)" package="3 mm [THT]"]
  LED8 = LED - 3mm [color="Green (555nm)" package="3 mm [THT]"]
  LED9 = LED - 3mm [color="White (6500K)" package="3 mm [THT]"]
  LED10 = LED - 3mm [color="White (6500K)" package="3 mm [THT]"]
  LED11 = LED - 3mm [color="White (6500K)" package="3 mm [THT]"]
  LED12 = LED - 3mm [color="White (6500K)" package="3 mm [THT]"]
  LED13 = LED - 3mm [color="White (6500K)" package="3 mm [THT]"]
  U1 = attiny85 [package=dip]
  R14 = Resistor [tolerance=±5% resistance=200 package=THT]
  R15 = Resistor [tolerance=±5% resistance=200 package=THT]

nets:
  N1: Q1.E, LED9.cathode, LED10.cathode, LED11.cathode, LED12.cathode, LED13.cathode
  N2: Q1.B, R15.Pin_1
  N3: Q1.C, Q2.C
  N4: Q2.E, LED1.cathode, LED2.cathode, LED3.cathode, LED4.cathode, LED5.cathode, LED6.cathode, LED7.cathode, LED8.cathode
  N5: Q2.B, R14.Pin_1
  N6: R1.Pin_0, R2.Pin_0, R3.Pin_0, R4.Pin_0, R5.Pin_0, R6.Pin_0, R7.Pin_0, R8.Pin_0, R9.Pin_0, R10.Pin_0, R11.Pin_0, R12.Pin_0, R13.Pin_0
  N7: R1.Pin_1, LED4.anode
  N8: R2.Pin_1, LED3.anode
  N9: R3.Pin_1, LED2.anode
  N10: R4.Pin_1, LED1.anode
  N11: R5.Pin_1, LED5.anode
  N12: R6.Pin_1, LED6.anode
  N13: R7.Pin_1, LED7.anode
  N14: R8.Pin_1, LED8.anode
  N15: R9.Pin_1, LED9.anode
  N16: R10.Pin_1, LED10.anode
  N17: R11.Pin_1, LED11.anode
  N18: R12.Pin_1, LED12.anode
  N19: R13.Pin_1, LED13.anode
  N20: U1.Pin_5, R15.Pin_0
  N21: U1.Pin_6, R14.Pin_0
